// Logisim project Code_lines.circ as structural Verilog: 1 circuit, main circuit main
module main (
  input  C_0,
  input  C_1,
  output D_00,
  output D_10,
  output D_01,
  output D_11
);

  wire not_1_out, not_2_out;

  not not_1 (not_1_out, C_0);
  not not_2 (not_2_out, C_1);
  and and_1 (D_00, not_1_out, not_2_out);
  and and_2 (D_10, C_0, not_2_out);
  and and_3 (D_01, not_1_out, C_1);
  and and_4 (D_11, C_0, C_1);
endmodule
