// Logisim project Odd_OR_even.circ as structural Verilog: 1 circuit, main circuit main
module main (
  input  x_0,
  input  x_1,
  input  x_2,
  input  y_0,
  input  y_1,
  input  y_2,
  output out_7
);

  wire and_1_out, and_2_out, not_1_out, not_2_out, or_1_out;

  not not_1 (not_1_out, x_0);
  not not_2 (not_2_out, y_0);
  and and_1 (and_1_out, not_1_out, y_0);
  and and_2 (and_2_out, x_0, not_2_out);
  or or_1 (or_1_out, and_1_out, and_2_out);
  not not_3 (out_7, or_1_out);

  // Notes on the sheet:
  //   The y group
  //   The x group
  //   To clarify, only the 0th bit matters. 
  //   because the other factors are 2^n. We can only care about the 0th
  //   If 0 is off, then the product is even
  //   Two odd numbers make an even number as do two even
  //   However, an odd and an even produce an odd. 
  //   This, the gate we desire is XNOR
endmodule
