// Logisim project fixed_hw1q3.circ as structural Verilog: 1 circuit, main circuit main
// ACD
module main (
  input  A,
  input  B,
  input  C,
  input  D,
  output out_5
);

  wire ABC_out, ACD_out, BCD_out, not_1_out, not_2_out, not_3_out, not_4_out, Only_A_out, Only_B_out,
       Only_C_out, Only_D_out, or_1_out;

  not not_1 (not_1_out, A);
  not not_2 (not_2_out, B);
  not not_3 (not_3_out, C);
  not not_4 (not_4_out, D);
  and Only_D (Only_D_out, not_1_out, not_2_out, not_3_out, D);
  and Only_C (Only_C_out, not_1_out, not_2_out, C, not_4_out);
  and Only_B (Only_B_out, not_1_out, B, not_3_out, not_4_out);
  and Only_A (Only_A_out, A, not_2_out, not_3_out, not_4_out);
  and ABC (ABC_out, A, B, C, not_4_out);
  and BCD (BCD_out, not_1_out, B, C, D);
  and ACD (ACD_out, A, not_2_out, C, D);
  // AND_Gate ABD has open pins: in0=A, in1=B, in3=not_3_out, in4=D, out=open
  or or_1 (or_1_out, ABC_out, BCD_out, ACD_out);
  or or_2 (out_5, Only_D_out, Only_C_out, Only_B_out, Only_A_out, or_1_out);
endmodule
