// Logisim project ALU.circ as structural Verilog: 7 circuits, main circuit main
module main (
  input  X_3,
  input  X_2,
  input  X_1,
  input  x_0,
  input  y_3,
  input  y_2,
  input  y_1,
  input  y_0,
  input  ZX,
  input  ZY,
  input  NX,
  input  NY,
  input  F_x_y,
  input  NO,
  output Output_0,
  output Output_1,
  output Output_2,
  output Output_3
);

  wire clear_1_out_0, clear_1_out_1, clear_1_out_2, clear_1_out_3, clear_2_out_0, clear_2_out_1,
       clear_2_out_2, clear_2_out_3, negate_1_out_0, negate_1_out_1, negate_1_out_2, negate_1_out_3,
       negate_3_out_0, negate_3_out_1, negate_3_out_2, negate_3_out_3, the_f_part_1_out_0,
       the_f_part_1_out_1, the_f_part_1_out_2, the_f_part_1_out_3;

  clear clear_1 (
    .Control(ZX), .In_3(X_3), .In_2(X_2), .In_1(X_1), .In_0(x_0), .Out_3(clear_1_out_3),
    .Out_2(clear_1_out_2), .Out_1(clear_1_out_1), .Out_0(clear_1_out_0));
  Negate negate_1 (
    .Control(NX), .In_3(clear_1_out_3), .In_2(clear_1_out_2), .In_1(clear_1_out_1), .In_0(clear_1_out_0),
    .Out_3(negate_1_out_3), .Out_2(negate_1_out_2), .Out_1(negate_1_out_1), .Out_0(negate_1_out_0));
  The_f_part the_f_part_1 (
    .Control(F_x_y), .X_3(negate_1_out_3), .X_2(negate_1_out_2), .X_1(negate_1_out_1), .x_0(negate_1_out_0),
    .y_3(negate_3_out_3), .y_2(negate_3_out_2), .y_1(negate_3_out_1), .y_0(negate_3_out_0),
    .Out_3(the_f_part_1_out_3), .Out_2(the_f_part_1_out_2), .out_1(the_f_part_1_out_1),
    .out_0(the_f_part_1_out_0));
  Negate negate_2 (
    .Control(NO), .In_3(the_f_part_1_out_3), .In_2(the_f_part_1_out_2), .In_1(the_f_part_1_out_1),
    .In_0(the_f_part_1_out_0), .Out_3(Output_3), .Out_2(Output_2), .Out_1(Output_1), .Out_0(Output_0));
  clear clear_2 (
    .Control(ZY), .In_3(y_3), .In_2(y_2), .In_1(y_1), .In_0(y_0), .Out_3(clear_2_out_3),
    .Out_2(clear_2_out_2), .Out_1(clear_2_out_1), .Out_0(clear_2_out_0));
  Negate negate_3 (
    .Control(NY), .In_3(clear_2_out_3), .In_2(clear_2_out_2), .In_1(clear_2_out_1), .In_0(clear_2_out_0),
    .Out_3(negate_3_out_3), .Out_2(negate_3_out_2), .Out_1(negate_3_out_1), .Out_0(negate_3_out_0));

  // Notes on the sheet:
  //   Clear x
  //   Negate x
  //   F function
  //   Negate output
  //   Clear y
  //   Negate y
endmodule

module add (
  input  in_1,
  input  in_0,
  output Carry,
  output Out
);

  and and_1 (Carry, in_1, in_0);
  xor xor_1 (Out, in_1, in_0);

  // Notes on the sheet:
  //   If both on then carry
  //   If only one bit then returns one
endmodule

module Negate (
  input  In_3,
  input  In_2,
  input  In_1,
  input  In_0,
  input  Control,
  output Out_0,
  output Out_1,
  output Out_2,
  output Out_3
);

  wire add_2_carry, add_3_carry, add_4_carry, xor_1_out, xor_2_out, xor_3_out, xor_4_out;

  xor xor_1 (xor_1_out, Control, In_3);
  xor xor_2 (xor_2_out, Control, In_2);
  add add_1 (.in_1(xor_1_out), .in_0(add_3_carry), .Out(Out_3));  // open: Carry
  xor xor_3 (xor_3_out, Control, In_1);
  add add_2 (.in_1(xor_3_out), .in_0(add_4_carry), .Carry(add_2_carry), .Out(Out_1));
  add add_3 (.in_1(xor_2_out), .in_0(add_2_carry), .Carry(add_3_carry), .Out(Out_2));
  xor xor_4 (xor_4_out, Control, In_0);
  add add_4 (.in_1(1'b0), .in_0(xor_4_out), .Carry(add_4_carry), .Out(Out_0));

  // Notes on the sheet:
  //   Originally twos comp
  //   can be made into twos by
  //   connecting to control
  //   carry
  //   Adds one when control on
  //   flips bit
endmodule

module clear (
  input  In_3,
  input  In_2,
  input  In_1,
  input  In_0,
  input  Control,
  output Out_3,
  output Out_2,
  output Out_1,
  output Out_0
);

  wire not_1_out;

  not not_1 (not_1_out, Control);
  and and_1 (Out_3, not_1_out, In_3);
  and and_2 (Out_2, not_1_out, In_2);
  and and_3 (Out_1, not_1_out, In_1);
  and and_4 (Out_0, not_1_out, In_0);
endmodule

// Adding bits
module _4_and_4_bit_add (
  input  X_3,
  input  X_2,
  input  X_1,
  input  x_0,
  input  y_3,
  input  y_2,
  input  y_1,
  input  y_0,
  output out_0,
  output out_1,
  output Out_2,
  output Out_3
);

  wire add_1_out, add_2_out, add_4_carry, add_4_out, add_5_carry, add_5_out, add_6_carry, add_7_out,
       add_8_carry, add_9_carry;

  add add_1 (.in_1(X_3), .in_0(y_3), .Out(add_1_out));  // open: Carry
  add add_2 (.in_1(add_1_out), .in_0(add_5_carry), .Out(add_2_out));  // open: Carry
  add add_3 (.in_1(add_2_out), .in_0(add_8_carry), .Out(Out_3));  // open: Carry
  add add_4 (.in_1(X_1), .in_0(y_1), .Carry(add_4_carry), .Out(add_4_out));
  add add_5 (.in_1(X_2), .in_0(y_2), .Carry(add_5_carry), .Out(add_5_out));
  add add_6 (.in_1(add_4_out), .in_0(add_9_carry), .Carry(add_6_carry), .Out(out_1));
  add add_7 (.in_1(add_4_carry), .in_0(add_6_carry), .Out(add_7_out));  // open: Carry
  add add_8 (.in_1(add_5_out), .in_0(add_7_out), .Carry(add_8_carry), .Out(Out_2));
  add add_9 (.in_1(x_0), .in_0(y_0), .Carry(add_9_carry), .Out(out_0));

  // Notes on the sheet:
  //   I used the previously made half adder
  //   to avoid redundency
  //   First carry bit add
  //   Intial bit add layer
endmodule

module The_f_part (
  input  X_3,
  input  X_2,
  input  X_1,
  input  x_0,
  input  y_3,
  input  y_2,
  input  y_1,
  input  y_0,
  input  Control,
  output Out_3,
  output Out_2,
  output out_1,
  output out_0
);

  wire clear_1_out_0, clear_1_out_1, clear_1_out_2, clear_1_out_3, clear_2_out_0, clear_2_out_1,
       clear_2_out_2, clear_2_out_3, n4_and_4_and_1_out_0, n4_and_4_and_1_out_1, n4_and_4_and_1_out_2,
       n4_and_4_and_1_out_3, n4_and_4_bit_add_1_out_0, n4_and_4_bit_add_1_out_1, n4_and_4_bit_add_1_out_2,
       n4_and_4_bit_add_1_out_3, not_1_out;

  _4_and_4_AND u_4_and_4_and_1 (
    .X_3(X_3), .X_2(X_2), .X_1(X_1), .x_0(x_0), .y_3(y_3), .y_2(y_2), .y_1(y_1), .y_0(y_0),
    .Out_3(n4_and_4_and_1_out_3), .Out_2(n4_and_4_and_1_out_2), .out_1(n4_and_4_and_1_out_1),
    .out_0(n4_and_4_and_1_out_0));
  clear clear_1 (
    .Control(Control), .In_3(n4_and_4_and_1_out_3), .In_2(n4_and_4_and_1_out_2), .In_1(n4_and_4_and_1_out_1),
    .In_0(n4_and_4_and_1_out_0), .Out_3(clear_1_out_3), .Out_2(clear_1_out_2), .Out_1(clear_1_out_1),
    .Out_0(clear_1_out_0));
  or or_1 (Out_3, clear_1_out_3, clear_2_out_3);
  or or_2 (Out_2, clear_1_out_2, clear_2_out_2);
  _4_and_4_bit_add u_4_and_4_bit_add_1 (
    .X_3(X_3), .X_2(X_2), .X_1(X_1), .x_0(x_0), .y_3(y_3), .y_2(y_2), .y_1(y_1), .y_0(y_0),
    .Out_3(n4_and_4_bit_add_1_out_3), .Out_2(n4_and_4_bit_add_1_out_2), .out_1(n4_and_4_bit_add_1_out_1),
    .out_0(n4_and_4_bit_add_1_out_0));
  not not_1 (not_1_out, Control);
  or or_3 (out_1, clear_1_out_1, clear_2_out_1);
  clear clear_2 (
    .Control(not_1_out), .In_3(n4_and_4_bit_add_1_out_3), .In_2(n4_and_4_bit_add_1_out_2),
    .In_1(n4_and_4_bit_add_1_out_1), .In_0(n4_and_4_bit_add_1_out_0), .Out_3(clear_2_out_3),
    .Out_2(clear_2_out_2), .Out_1(clear_2_out_1), .Out_0(clear_2_out_0));
  or or_4 (out_0, clear_1_out_0, clear_2_out_0);
endmodule

// And Bits
module _4_and_4_AND (
  input  X_3,
  input  X_2,
  input  X_1,
  input  x_0,
  input  y_3,
  input  y_2,
  input  y_1,
  input  y_0,
  output out_0,
  output out_1,
  output Out_3,
  output Out_2
);

  and and_1 (Out_3, X_3, y_3);
  and and_2 (out_1, X_1, y_1);
  and and_3 (Out_2, X_2, y_2);
  and and_4 (out_0, x_0, y_0);
endmodule
