// Logisim project Parity_Niels_Taylor.circ as structural Verilog: 1 circuit, main circuit main
module main (
  input  a,
  input  b,
  input  c,
  output out_4
);

  wire and_1_out, and_2_out, and_3_out, and_4_out, not_1_out, not_2_out, not_3_out, not_4_out, or_1_out,
       or_2_out;

  not not_1 (not_1_out, a);
  not not_2 (not_2_out, a);
  and and_1 (and_1_out, a, a, a);
  and and_2 (and_2_out, not_1_out, not_2_out);
  or or_1 (or_1_out, and_1_out, and_2_out);
  and and_3 (and_3_out, or_1_out, c);
  not not_3 (not_3_out, or_1_out);
  and and_4 (and_4_out, not_3_out, not_4_out);
  not not_4 (not_4_out, c);
  or or_2 (or_2_out, and_3_out, and_4_out);
  not not_5 (out_4, or_2_out);

  assign b = a;
endmodule
