// Logisim project mux4_Niels_Taylor.circ as structural Verilog: 1 circuit, main circuit main
module main (
  input  Line_selection_0,
  input  Line_selection_1,
  input  Input_0,
  input  INput_1,
  input  Input_2,
  input  INput_3,
  output out_7
);

  wire and_1_out, and_2_out, and_3_out, and_4_out, not_1_out, not_2_out, not_3_out, not_4_out;

  not not_1 (not_1_out, Line_selection_0);
  not not_2 (not_2_out, Line_selection_1);
  and and_1 (and_1_out, not_1_out, not_2_out, Input_0);
  and and_2 (and_2_out, Line_selection_0, not_3_out, INput_1);
  not not_3 (not_3_out, Line_selection_1);
  not not_4 (not_4_out, Line_selection_0);
  and and_3 (and_3_out, not_4_out, Line_selection_1, Input_2);
  and and_4 (and_4_out, Line_selection_0, Line_selection_1, INput_3);
  or or_1 (out_7, and_1_out, and_2_out, and_3_out, and_4_out);
endmodule
