// Logisim project lab2QuinnH_TaylorB.circ as structural Verilog
module _4bit_neg (
  input  a3,
  input  a2,
  input  a1,
  input  a0,
  output o_0,
  output _0_1,
  output o_2,
  output o_3
);

  wire adder_1_cout, adder_2_cout, adder_3_cout, not_1_out, not_2_out, not_3_out, not_4_out;

  not not_1 (not_1_out, a3);
  not not_2 (not_2_out, a2);
  not not_3 (not_3_out, a1);
  not not_4 (not_4_out, a0);
  Adder #(.width(1)) adder_1 (.a(not_4_out), .b(1'b1), .out(o_0), .cout(adder_1_cout));  // open: cin
  Adder #(.width(1)) adder_2 (.a(adder_1_cout), .b(not_3_out), .out(_0_1), .cout(adder_2_cout));  // open: cin
  Adder #(.width(1)) adder_3 (.a(adder_2_cout), .b(not_2_out), .out(o_2), .cout(adder_3_cout));  // open: cin
  Adder #(.width(1)) adder_4 (.a(adder_3_cout), .b(not_1_out), .out(o_3));  // open: cin, cout
endmodule

module subtraction (
  input  b_3,
  input  b_2,
  input  b_1,
  input  b_0,
  input  a_0,
  input  a_1,
  input  a_2,
  input  a_3,
  output o_0,
  output o_1,
  output o_2,
  output o_3
);

  wire adder_1_cout, adder_2_cout, adder_3_cout, n4bit_neg_1__0_1, n4bit_neg_1_o_0, n4bit_neg_1_o_2,
       n4bit_neg_1_o_3;

  _4bit_neg u_4bit_neg_1 (
    .a3(b_3), .a2(b_2), .a1(b_1), .a0(b_0), .o_0(n4bit_neg_1_o_0), ._0_1(n4bit_neg_1__0_1),
    .o_2(n4bit_neg_1_o_2), .o_3(n4bit_neg_1_o_3));
  Adder #(.width(1)) adder_1 (.a(n4bit_neg_1_o_0), .b(a_0), .out(o_0), .cout(adder_1_cout));  // open: cin
  Adder #(.width(1)) adder_2 (.a(n4bit_neg_1__0_1), .b(a_1), .out(o_1), .cin(adder_1_cout), .cout(adder_2_cout));
  Adder #(.width(1)) adder_3 (.a(n4bit_neg_1_o_2), .b(a_2), .out(o_2), .cin(adder_2_cout), .cout(adder_3_cout));
  Adder #(.width(1)) adder_4 (.a(n4bit_neg_1_o_3), .b(a_3), .out(o_3), .cin(adder_3_cout));  // open: cout
endmodule

module comparison (
  input  b_3,
  input  b_2,
  input  b_1,
  input  b_0,
  input  a_0,
  input  a_1,
  input  a_2,
  input  a_3,
  output out_9
);

  wire not_1_out, subtraction_1_p9;

  not not_1 (not_1_out, subtraction_1_p9);
  // subtraction subtraction_1: pin names not known; wires that end beside it: a_0, a_1, a_2, a_3, b_3, b_2, b_1, b_0, subtraction_1_p9
  buf and_1 (out_9, not_1_out);  // AND_Gate
endmodule
