// Logisim project Half_adder.circ as structural Verilog: 1 circuit, main circuit main
module main (
  input  x,
  input  in_2,
  output out_3,
  output Carry
);

  wire and_1_out, and_2_out, not_1_out, not_2_out;

  not not_1 (not_1_out, x);
  not not_2 (not_2_out, in_2);
  and and_1 (and_1_out, in_2, not_1_out);
  and and_2 (and_2_out, x, not_2_out);
  and and_3 (Carry, in_2, x);
  or or_1 (out_3, and_1_out, and_2_out);
endmodule
